// Digital circuit frontpanel.dig as structural Verilog
module frontpanel (
  input  clock,
  output [15:0] R0,
  output [15:0] R1,
  output [15:0] R2,
  output [15:0] R3,
  output [3:0] PC,
  output halt,
  output error
);

  wire add, advance_out, hex, hexdisplay_1_p2, hexdisplay_1_p3, hexdisplay_1_p5, hexdisplay_1_p8,
       hexdisplay_1_p10, hexdisplay_1_p13, hexdisplay_2_p2, hexdisplay_2_p5, hexdisplay_2_p8,
       hexdisplay_2_p10, hexdisplay_2_p13, instrdisplay_1_p1, instrdisplay_1_p2, instrdisplay_1_p3,
       instrdisplay_1_p4, instrdisplay_1_p5, instrdisplay_1_p6, jump, L, move, or_1_out, pmshim_1_c,
       pmshim_1_l, pmshim_1_s, R, regdisplay_1_p1, regdisplay_1_p2, regdisplay_2_p1, regdisplay_2_p2, tworeg;
  wire [1:0] rd, rs;
  wire [3:0] hexdisplay_1_p1, hexdisplay_1_p4, hexdisplay_1_p6, hexdisplay_1_p9, hexdisplay_1_p12,
       hexdisplay_2_p1, hexdisplay_2_p4, hexdisplay_2_p6, hexdisplay_2_p9, hexdisplay_2_p12, pmshim_1_a;
  wire [4:0] op;
  wire [15:0] decoder_1_p1, decoder_1_p2, execute_1_p4, fetch_1_instr_o, instrdisplay_1_d1,
       instrdisplay_1_d2, instrdisplay_1_d3, instrdisplay_1_d4, instrdisplay_1_d5, instrdisplay_1_d6,
       pmshim_1_d, Program_d, regdisplay_1_d1, regdisplay_1_d2, regdisplay_2_d1, regdisplay_2_d2;

  pmshim pmshim_1 (.pc(PC), .A(pmshim_1_a), .D(pmshim_1_d), .s(pmshim_1_s), .C(pmshim_1_c), .L(pmshim_1_l));
  Button advance (.out(advance_out));
  SixteenSeg sixteenseg_1 (.led(regdisplay_1_d1), .dp(regdisplay_1_p1));
  regdisplay regdisplay_1 (
    .D1(regdisplay_1_d1), .P1(regdisplay_1_p1), .D2(regdisplay_1_d2), .P2(regdisplay_1_p2), .E(1'b1),
    .J(jump), .R(rd));
  EEPROMDualPort #(.AddrBits(4), .isProgramMemory("true"), .Bits(16)) Program (
    .A(pmshim_1_a), .Din(pmshim_1_d), .str(pmshim_1_s), .C(pmshim_1_c), .ld(pmshim_1_l), .D(Program_d));
  or or_1 (or_1_out, advance_out, clock);
  SixteenSeg sixteenseg_2 (.led(regdisplay_1_d2), .dp(regdisplay_1_p2));
  Seven_Seg_Hex seven_seg_hex_1 (.d(hexdisplay_1_p1), .dp(hexdisplay_1_p2));
  Seven_Seg_Hex seven_seg_hex_2 (.d(hexdisplay_1_p4), .dp(hexdisplay_1_p5));
  // hexdisplay hexdisplay_1: pin names not known; wires that end beside it: hexdisplay_1_p1, hexdisplay_1_p2, hexdisplay_1_p3, hexdisplay_1_p4, hexdisplay_1_p5, hexdisplay_1_p6, L, hexdisplay_1_p8, hexdisplay_1_p9, hexdisplay_1_p10, hex, hexdisplay_1_p12, hexdisplay_1_p13
  fetch fetch_1 (
    .instr_i(Program_d), .clock(or_1_out), .en(R), .jump(jump), .pc(PC), .instr_o(fetch_1_instr_o));  // open: value
  Seven_Seg_Hex seven_seg_hex_3 (.d(hexdisplay_1_p6), .dp(hexdisplay_1_p8));
  Seven_Seg_Hex seven_seg_hex_4 (.d(hexdisplay_1_p9), .dp(hexdisplay_1_p10));
  not not_1 (hexdisplay_1_p3, jump);
  Seven_Seg_Hex seven_seg_hex_5 (.d(hexdisplay_1_p12), .dp(hexdisplay_1_p13));
  // decoder decoder_1: pin names not known; wires that end beside it: decoder_1_p1, decoder_1_p2, fetch_1_instr_o, rs, rd, L, R, op, tworeg, move, add, jump
  SixteenSeg sixteenseg_3 (.led(instrdisplay_1_d1), .dp(instrdisplay_1_p1));
  instrdisplay instrdisplay_1 (
    .D1(instrdisplay_1_d1), .P1(instrdisplay_1_p1), .D2(instrdisplay_1_d2), .P2(instrdisplay_1_p2),
    .D3(instrdisplay_1_d3), .P3(instrdisplay_1_p3), .D4(instrdisplay_1_d4), .P4(instrdisplay_1_p4),
    .D5(instrdisplay_1_d5), .P5(instrdisplay_1_p5), .D6(instrdisplay_1_d6), .P6(instrdisplay_1_p6), .I(op));
  SixteenSeg sixteenseg_4 (.led(instrdisplay_1_d2), .dp(instrdisplay_1_p2));
  SixteenSeg sixteenseg_5 (.led(instrdisplay_1_d3), .dp(instrdisplay_1_p3));
  SixteenSeg sixteenseg_6 (.led(instrdisplay_1_d4), .dp(instrdisplay_1_p4));
  SixteenSeg sixteenseg_7 (.led(instrdisplay_1_d5), .dp(instrdisplay_1_p5));
  SixteenSeg sixteenseg_8 (.led(instrdisplay_1_d6), .dp(instrdisplay_1_p6));
  DipSwitch u_hex (.out(hex));
  // execute execute_1: pin names not known; wires that end beside it: L, R, op, execute_1_p4, halt, error
  Seven_Seg_Hex seven_seg_hex_6 (.d(hexdisplay_2_p1), .dp(hexdisplay_2_p2));
  Seven_Seg_Hex seven_seg_hex_7 (.d(hexdisplay_2_p4), .dp(hexdisplay_2_p5));
  // hexdisplay hexdisplay_2: pin names not known; wires that end beside it: hexdisplay_2_p1, hexdisplay_2_p2, 1'b1, hexdisplay_2_p4, hexdisplay_2_p5, hexdisplay_2_p6, R, hexdisplay_2_p8, hexdisplay_2_p9, hexdisplay_2_p10, hex, hexdisplay_2_p12, hexdisplay_2_p13
  Seven_Seg_Hex seven_seg_hex_8 (.d(hexdisplay_2_p6), .dp(hexdisplay_2_p8));
  Seven_Seg_Hex seven_seg_hex_9 (.d(hexdisplay_2_p9), .dp(hexdisplay_2_p10));
  Seven_Seg_Hex seven_seg_hex_10 (.d(hexdisplay_2_p12), .dp(hexdisplay_2_p13));
  regfile regfile_1 (
    .rs(rs), .rd(rd), .result(execute_1_p4), .clock(or_1_out), .rdval(decoder_1_p1), .rsval(decoder_1_p2),
    .R0(R0), .R1(R1), .R2(R2), .R3(R3));
  SixteenSeg sixteenseg_9 (.led(regdisplay_2_d1), .dp(regdisplay_2_p1));
  regdisplay regdisplay_2 (
    .D1(regdisplay_2_d1), .P1(regdisplay_2_p1), .D2(regdisplay_2_d2), .P2(regdisplay_2_p2), .E(tworeg),
    .J(1'b0), .R(rs));
  SixteenSeg sixteenseg_10 (.led(regdisplay_2_d2), .dp(regdisplay_2_p2));

  // Notes on the sheet:
  //   contents of Program (hex, n*v repeats v):
  //   120,61,bd,91,7d,10e
  //   rj45 Creates
endmodule
